# Fritzing sketch light_board (saved by Fritzing 0.9.3b)
perfboards: 1

parts:
  J1 = screw terminal, 3 pins
  J2 = screw terminal, 3 pins
  J3 = screw terminal, 3 pins
  J4 = screw terminal, 3 pins
  U1 = ESP8266 WiFi Module [part_number=ESP8266]
  U2 = Voltage Regulator - 3.3V [package="TO220 [THT]"]
  R1 = Resistor [tolerance=±5% resistance=10k package=THT]
  R2 = Resistor [tolerance=±5% resistance=10k package=THT]
  R3 = Resistor [tolerance=±5% resistance=10k package=THT]
  R4 = Resistor [tolerance=±5% resistance=10k package=THT]
  R5 = Resistor [tolerance=±5% resistance=10k package=THT]
  R6 = Resistor [tolerance=±5% resistance=300 package=THT]
  S1 = Pushbutton [package="[THT]"]
  S2 = Pushbutton [package="[THT]"]
  R7 = Resistor [tolerance=±5% resistance=300 package=THT]

nets:
  N1: J1.pin1, J2.pin1, J3.pin1, J4.pin1, U1.GND, U2.input_voltage, R1.Pin_1, S1.Pin_3, S1.Pin_4, S2.Pin_1, S2.Pin_2
  N2: J1.pin3, U1.GPIO_12
  N3: J2.pin3, U1.GPIO_4
  N4: J3.pin3, U1.GPIO_5
  N5: J4.pin3, U1.GPIO_14
  N6: U1.VCC, U2.output_voltage, R2.Pin_1, R3.Pin_1, R4.Pin_1, R5.Pin_1
  N7: U1.GPIO_0, R4.Pin_0, R7.Pin_0
  N8: U1.GPIO_2, R5.Pin_0
  N9: U1.CH_PD, R3.Pin_0
  N10: U1.GPIO_15, R1.Pin_0
  N11: U1.REST, R2.Pin_0, R6.Pin_1
  N12: R6.Pin_0, S1.Pin_1, S1.Pin_2
  N13: S2.Pin_3, S2.Pin_4, R7.Pin_1

notes:
  220V door
  220V hangar
  220V inner 1
  220V inner 2
  Gnd
  3v3
  Reset
  Burn
